# Fritzing sketch night-light (saved by Fritzing 1.0.3b)
breadboards: 1

parts:
  Part1 = Arduino Mega 2560 (Rev3)
  R1 = PHOTOCELL [package=photocell-kit]
  R2 = Resistor [tolerance=±5% power=0.25W resistance=220 package=THT]
  LED2 = LED - 5mm [color="Red (633nm)" current=0.030A package="5 mm [THT]"]
  R3 = Resistor [tolerance=±5% power=0.25W resistance=220 package=THT]

nets:
  N1: Part1.A0, R1.P$2, R2.Pin_1
  N2: Part1.5V, R1.P$1
  N3: Part1.GND, R2.Pin_0, R3.Pin_0
  N4: Part1.D7_PWM, LED2.cathode
  N5: LED2.anode, R3.Pin_1

// code stored in the sketch: night-light.ino
void setup()
{
 Serial.begin(9600);
 pinMode(7,OUTPUT) ;
 pinMode(A0,INPUT) ;
}


void loop()
{
    //getting the value of the LDR
  int c = analogRead(A0) ;


  Serial.println(c) ;


    //if the value of the LDR is less than 500, the LED will turn on
  if(c<500)
  {
    digitalWrite(7,HIGH) ; 
  }
  else
  {
    digitalWrite(7,LOW) ; 
  }
}
